// Logisim project PHANTOM_32.circ as structural Verilog
module alu (
  input  [3:0] op,
  input  [31:0] lhs,
  input  [31:0] rhs,
  output [31:0] result
);

  wire [0:0] comparator_1_lt, comparator_2_lt;
  wire [31:0] adder_1_out, and_1_out, nor_1_out, or_1_out, shifter_1_out, shifter_2_out, shifter_3_out,
       subtractor_1_out;

  Adder #(.width(32)) adder_1 (.a(lhs), .b(rhs), .out(adder_1_out), .cin(1'b0));  // open: cout
  Subtractor #(.width(32)) subtractor_1 (.a(lhs), .b(rhs), .out(subtractor_1_out), .bin(1'b0));  // open: bout
  assign and_1_out = lhs & rhs;  // AND_Gate and_1, 32 bits wide
  assign or_1_out = lhs | rhs;  // OR_Gate or_1, 32 bits wide
  assign nor_1_out = ~(lhs | rhs);  // NOR_Gate nor_1, 32 bits wide
  Shifter #(.width(32)) shifter_1 (.in(lhs), .\dist (rhs[4:0]), .out(shifter_1_out));
  Shifter #(.shift("lr"), .width(32)) shifter_2 (.in(lhs), .\dist (rhs[4:0]), .out(shifter_2_out));
  Shifter #(.shift("ar"), .width(32)) shifter_3 (.in(lhs), .\dist (rhs[4:0]), .out(shifter_3_out));
  Comparator #(.width(32)) comparator_1 (.a(lhs), .b(rhs), .lt(comparator_1_lt[0]));  // open: gt, eq
  Comparator #(.mode("unsigned"), .width(32)) comparator_2 (.a(lhs), .b(rhs), .lt(comparator_2_lt[0]));  // open: gt, eq
  Multiplexer #(.select(4), .width(32)) multiplexer_1 (
    .in0(adder_1_out), .in1(subtractor_1_out), .in2(and_1_out), .in3(or_1_out), .in4(nor_1_out),
    .in5(shifter_1_out), .in6(shifter_2_out), .in7(shifter_3_out), .in8({{31{1'b0}}, comparator_1_lt[0]}),
    .in9({{31{1'b0}}, comparator_2_lt[0]}), .in10(rhs), .in11(32'hdeadbeef), .in12(32'hdeadbeef),
    .in13(32'hdeadbeef), .in14(32'hdeadbeef), .in15(32'hdeadbeef), .out(result));  // open: sel
endmodule

module regfile (
  input  [4:0] rd_index_b,
  input  [4:0] rd_index_a,
  input  [4:0] wr_index,
  input  [31:0] wr_data,
  input  wr_en,
  input  clk,
  output [31:0] rd_data_b,
  output [31:0] rd_data_a
);

  wire and_2_out, and_3_out, and_4_out, and_5_out, and_6_out, and_7_out, and_8_out, and_9_out, and_10_out,
       and_11_out, and_12_out, and_13_out, and_14_out, and_15_out, and_16_out, and_17_out, and_18_out,
       and_19_out, and_20_out, and_21_out, and_22_out, and_23_out, and_24_out, and_25_out, and_26_out,
       and_27_out, and_28_out, and_29_out, and_30_out, and_31_out, and_32_out;
  wire [31:0] decoder_1_out0, register_1_q, register_2_q, register_3_q, register_4_q, register_5_q,
       register_6_q, register_7_q, register_8_q, register_9_q, register_10_q, register_11_q, register_12_q,
       register_13_q, register_14_q, register_15_q, register_16_q, register_17_q, register_18_q,
       register_19_q, register_20_q, register_21_q, register_22_q, register_23_q, register_24_q,
       register_25_q, register_26_q, register_27_q, register_28_q, register_29_q, register_30_q,
       register_31_q, register_32_q;

  Decoder #(.enable("false"), .select(5)) decoder_1 (
    .out0(decoder_1_out0[0]), .out1(decoder_1_out0[1]), .out2(decoder_1_out0[2]), .out3(decoder_1_out0[3]),
    .out4(decoder_1_out0[4]), .out5(decoder_1_out0[5]), .out6(decoder_1_out0[6]), .out7(decoder_1_out0[7]),
    .out8(decoder_1_out0[8]), .out9(decoder_1_out0[9]), .out10(decoder_1_out0[10]),
    .out11(decoder_1_out0[11]), .out12(decoder_1_out0[12]), .out13(decoder_1_out0[13]),
    .out14(decoder_1_out0[14]), .out15(decoder_1_out0[15]), .out16(decoder_1_out0[16]),
    .out17(decoder_1_out0[17]), .out18(decoder_1_out0[18]), .out19(decoder_1_out0[19]),
    .out20(decoder_1_out0[20]), .out21(decoder_1_out0[21]), .out22(decoder_1_out0[22]),
    .out23(decoder_1_out0[23]), .out24(decoder_1_out0[24]), .out25(decoder_1_out0[25]),
    .out26(decoder_1_out0[26]), .out27(decoder_1_out0[27]), .out28(decoder_1_out0[28]),
    .out29(decoder_1_out0[29]), .out30(decoder_1_out0[30]), .out31(decoder_1_out0[31]), .sel(wr_index));
  Register #(.width(32)) register_1 (.D(wr_data), .clk(clk), .Q(register_1_q), .clr(1'b0));  // open: en
  // AND_Gate and_1 has open pins: in0=decoder_1_out0[0], in1=wr_en, out=open
  Register #(.width(32)) register_2 (.D(wr_data), .en(and_2_out), .clk(clk), .Q(register_2_q), .clr(1'b0));
  and and_2 (and_2_out, decoder_1_out0[1], wr_en);
  Register #(.width(32)) register_3 (.D(wr_data), .en(and_3_out), .clk(clk), .Q(register_3_q), .clr(1'b0));
  and and_3 (and_3_out, decoder_1_out0[2], wr_en);
  Register #(.width(32)) register_4 (.D(wr_data), .en(and_4_out), .clk(clk), .Q(register_4_q), .clr(1'b0));
  and and_4 (and_4_out, decoder_1_out0[3], wr_en);
  Register #(.width(32)) register_5 (.D(wr_data), .en(and_5_out), .clk(clk), .Q(register_5_q), .clr(1'b0));
  and and_5 (and_5_out, decoder_1_out0[4], wr_en);
  Register #(.width(32)) register_6 (.D(wr_data), .en(and_6_out), .clk(clk), .Q(register_6_q), .clr(1'b0));
  and and_6 (and_6_out, decoder_1_out0[5], wr_en);
  Register #(.width(32)) register_7 (.D(wr_data), .en(and_7_out), .clk(clk), .Q(register_7_q), .clr(1'b0));
  and and_7 (and_7_out, decoder_1_out0[6], wr_en);
  Register #(.width(32)) register_8 (.D(wr_data), .en(and_8_out), .clk(clk), .Q(register_8_q), .clr(1'b0));
  and and_8 (and_8_out, decoder_1_out0[7], wr_en);
  Register #(.width(32)) register_9 (.D(wr_data), .en(and_9_out), .clk(clk), .Q(register_9_q), .clr(1'b0));
  and and_9 (and_9_out, decoder_1_out0[8], wr_en);
  Register #(.width(32)) register_10 (.D(wr_data), .en(and_10_out), .clk(clk), .Q(register_10_q), .clr(1'b0));
  and and_10 (and_10_out, decoder_1_out0[9], wr_en);
  Register #(.width(32)) register_11 (.D(wr_data), .en(and_11_out), .clk(clk), .Q(register_11_q), .clr(1'b0));
  and and_11 (and_11_out, decoder_1_out0[10], wr_en);
  Register #(.width(32)) register_12 (.D(wr_data), .en(and_12_out), .clk(clk), .Q(register_12_q), .clr(1'b0));
  and and_12 (and_12_out, decoder_1_out0[11], wr_en);
  Register #(.width(32)) register_13 (.D(wr_data), .en(and_13_out), .clk(clk), .Q(register_13_q), .clr(1'b0));
  and and_13 (and_13_out, decoder_1_out0[12], wr_en);
  Register #(.width(32)) register_14 (.D(wr_data), .en(and_14_out), .clk(clk), .Q(register_14_q), .clr(1'b0));
  and and_14 (and_14_out, decoder_1_out0[13], wr_en);
  Register #(.width(32)) register_15 (.D(wr_data), .en(and_15_out), .clk(clk), .Q(register_15_q), .clr(1'b0));
  and and_15 (and_15_out, decoder_1_out0[14], wr_en);
  Register #(.width(32)) register_16 (.D(wr_data), .en(and_16_out), .clk(clk), .Q(register_16_q), .clr(1'b0));
  and and_16 (and_16_out, decoder_1_out0[15], wr_en);
  Register #(.width(32)) register_17 (.D(wr_data), .en(and_17_out), .clk(clk), .Q(register_17_q), .clr(1'b0));
  and and_17 (and_17_out, decoder_1_out0[16], wr_en);
  Register #(.width(32)) register_18 (.D(wr_data), .en(and_18_out), .clk(clk), .Q(register_18_q), .clr(1'b0));
  and and_18 (and_18_out, decoder_1_out0[17], wr_en);
  Register #(.width(32)) register_19 (.D(wr_data), .en(and_19_out), .clk(clk), .Q(register_19_q), .clr(1'b0));
  and and_19 (and_19_out, decoder_1_out0[18], wr_en);
  Register #(.width(32)) register_20 (.D(wr_data), .en(and_20_out), .clk(clk), .Q(register_20_q), .clr(1'b0));
  and and_20 (and_20_out, decoder_1_out0[19], wr_en);
  Register #(.width(32)) register_21 (.D(wr_data), .en(and_21_out), .clk(clk), .Q(register_21_q), .clr(1'b0));
  and and_21 (and_21_out, decoder_1_out0[20], wr_en);
  Register #(.width(32)) register_22 (.D(wr_data), .en(and_22_out), .clk(clk), .Q(register_22_q), .clr(1'b0));
  and and_22 (and_22_out, decoder_1_out0[21], wr_en);
  Register #(.width(32)) register_23 (.D(wr_data), .en(and_23_out), .clk(clk), .Q(register_23_q), .clr(1'b0));
  and and_23 (and_23_out, decoder_1_out0[22], wr_en);
  Register #(.width(32)) register_24 (.D(wr_data), .en(and_24_out), .clk(clk), .Q(register_24_q), .clr(1'b0));
  and and_24 (and_24_out, decoder_1_out0[23], wr_en);
  Register #(.width(32)) register_25 (.D(wr_data), .en(and_25_out), .clk(clk), .Q(register_25_q), .clr(1'b0));
  and and_25 (and_25_out, decoder_1_out0[24], wr_en);
  Register #(.width(32)) register_26 (.D(wr_data), .en(and_26_out), .clk(clk), .Q(register_26_q), .clr(1'b0));
  and and_26 (and_26_out, decoder_1_out0[25], wr_en);
  Register #(.width(32)) register_27 (.D(wr_data), .en(and_27_out), .clk(clk), .Q(register_27_q), .clr(1'b0));
  and and_27 (and_27_out, decoder_1_out0[26], wr_en);
  Register #(.width(32)) register_28 (.D(wr_data), .en(and_28_out), .clk(clk), .Q(register_28_q), .clr(1'b0));
  and and_28 (and_28_out, decoder_1_out0[27], wr_en);
  Register #(.width(32)) register_29 (.D(wr_data), .en(and_29_out), .clk(clk), .Q(register_29_q), .clr(1'b0));
  and and_29 (and_29_out, decoder_1_out0[28], wr_en);
  Register #(.width(32)) register_30 (.D(wr_data), .en(and_30_out), .clk(clk), .Q(register_30_q), .clr(1'b0));
  and and_30 (and_30_out, decoder_1_out0[29], wr_en);
  Register #(.width(32)) register_31 (.D(wr_data), .en(and_31_out), .clk(clk), .Q(register_31_q), .clr(1'b0));
  and and_31 (and_31_out, decoder_1_out0[30], wr_en);
  Register #(.width(32)) register_32 (.D(wr_data), .en(and_32_out), .clk(clk), .Q(register_32_q), .clr(1'b0));
  and and_32 (and_32_out, decoder_1_out0[31], wr_en);
  Multiplexer #(.select(5), .width(32)) multiplexer_1 (
    .in0({32{1'b0}}), .in1(register_2_q), .in2(register_3_q), .in3(register_4_q), .in4(register_5_q),
    .in5(register_6_q), .in6(register_7_q), .in7(register_8_q), .in8(register_9_q), .in9(register_10_q),
    .in10(register_11_q), .in11(register_12_q), .in12(register_13_q), .in13(register_14_q),
    .in14(register_15_q), .in15(register_16_q), .in16(register_17_q), .in17(register_18_q),
    .in18(register_19_q), .in19(register_20_q), .in20(register_21_q), .in21(register_22_q),
    .in22(register_23_q), .in23(register_24_q), .in24(register_25_q), .in25(register_26_q),
    .in26(register_27_q), .in27(register_28_q), .in28(register_29_q), .in29(register_30_q),
    .in30(register_31_q), .in31(register_32_q), .out(rd_data_b), .sel(rd_index_b));
  Multiplexer #(.select(5), .width(32)) multiplexer_2 (
    .in0({32{1'b0}}), .in1(register_2_q), .in2(register_3_q), .in3(register_4_q), .in4(register_5_q),
    .in5(register_6_q), .in6(register_7_q), .in7(register_8_q), .in8(register_9_q), .in9(register_10_q),
    .in10(register_11_q), .in11(register_12_q), .in12(register_13_q), .in13(register_14_q),
    .in14(register_15_q), .in15(register_16_q), .in16(register_17_q), .in17(register_18_q),
    .in18(register_19_q), .in19(register_20_q), .in20(register_21_q), .in21(register_22_q),
    .in22(register_23_q), .in23(register_24_q), .in24(register_25_q), .in25(register_26_q),
    .in26(register_27_q), .in27(register_28_q), .in28(register_29_q), .in29(register_30_q),
    .in30(register_31_q), .in31(register_32_q), .out(rd_data_a), .sel(rd_index_a));
endmodule

module csr_regfile (
  input  [31:0] trap_mtval,
  input  [31:0] trap_mcause,
  input  [31:0] trap_mepc,
  input  [31:0] wr_data,
  input  [11:0] rd_addr,
  input  wr_en,
  input  mret_en,
  input  trap_en,
  input  resetn,
  input  [11:0] wr_addr,
  input  clk,
  output [31:0] out_mstatus,
  output [31:0] out_mtvec,
  output [31:0] out_mepc,
  output [31:0] rd_data
);

  wire and_5_out, and_6_out, and_7_out, and_8_out, comparator_1_eq, comparator_2_eq, comparator_3_eq,
       comparator_4_eq, comparator_5_eq, comparator_6_eq, comparator_7_eq, comparator_8_eq, comparator_9_eq,
       comparator_10_eq, comparator_11_eq, multiplexer_4_out, multiplexer_5_out, priority_encoder_1_en_out,
       priority_encoder_1_gs;
  wire [1:0] multiplexer_1_out, priority_encoder_1_out;
  wire [31:0] and_1_out, and_2_out, and_3_out, and_4_out, MCAUSE_out, MEPC_out, MIE_out, MIP_out,
       MSCRATCH_out, MSTATUS_out, MTVAL_out, MTVEC_out, multiplexer_2_out, multiplexer_3_out,
       multiplexer_6_out, multiplexer_7_out, or_1_out, or_2_out, r_mie_q, r_mstatus_q;

  Priority_Encoder #(.select(2)) priority_encoder_1 (
    .in0(wr_en), .in1(mret_en), .in2(trap_en), .in3(resetn), .out(priority_encoder_1_out),
    .gs(priority_encoder_1_gs), .en_out(priority_encoder_1_en_out), .en_in(1'b1));
  Register #(.width(32)) r_mtvec ();  // open: D, en, clk, Q, clr
  Multiplexer #(.width(2)) multiplexer_1 (
    .in0(priority_encoder_1_out), .in1(2'b00), .out(multiplexer_1_out), .sel(priority_encoder_1_en_out));
  Register #(.width(32)) r_mscratch ();  // open: D, en, clk, Q, clr
  assign MSTATUS_out = r_mstatus_q & 32'hffffe777;  // AND_Gate MSTATUS, 32 bits wide
  assign and_1_out = r_mstatus_q & 32'h8;  // AND_Gate and_1, 32 bits wide
  assign and_2_out = r_mstatus_q & 32'hffffe777;  // AND_Gate and_2, 32 bits wide
  assign and_3_out = r_mstatus_q & 32'h80;  // AND_Gate and_3, 32 bits wide
  assign and_4_out = wr_data & 32'h1888;  // AND_Gate and_4, 32 bits wide
  Comparator #(.mode("unsigned"), .width(12)) comparator_1 (
    .a(12'h300), .b(rd_addr), .eq(comparator_1_eq));  // open: gt, lt
  and and_5 (and_5_out, comparator_1_eq, wr_en);
  and and_6 (and_6_out, priority_encoder_1_gs, ~multiplexer_1_out[1], ~multiplexer_1_out[0]);  // AND_Gate
  Comparator #(.mode("unsigned"), .width(12)) comparator_2 (
    .a(wr_addr), .b(12'h300), .eq(comparator_2_eq));  // open: gt, lt
  assign or_1_out = MSTATUS_out | {4'b0000, and_1_out[31:4]} | 32'h1800;  // OR_Gate or_1, 32 bits wide
  assign or_2_out = and_2_out | {4'b0000, and_3_out[31:4]} | 32'h1800;  // OR_Gate or_2, 32 bits wide
  Multiplexer #(.width(32)) multiplexer_2 (
    .in0(r_mstatus_q), .in1(and_4_out), .out(multiplexer_2_out), .sel(and_5_out));
  Multiplexer #(.select(2), .width(32)) multiplexer_3 (
    .in0(and_4_out), .in1(or_2_out), .in2(or_1_out), .in3(32'h1800), .out(multiplexer_3_out),
    .sel(multiplexer_1_out));
  Register #(.width(32)) r_mstatus (
    .D(multiplexer_3_out), .en(multiplexer_4_out), .clk(clk), .Q(r_mstatus_q), .clr(1'b0));
  Multiplexer multiplexer_4 (
    .in0(priority_encoder_1_gs), .in1(comparator_2_eq), .out(multiplexer_4_out), .sel(and_6_out));
  Register #(.width(32)) r_mepc ();  // open: D, en, clk, Q, clr
  assign MTVEC_out = 32'hfffffffd;  // AND_Gate MTVEC, 32 bits wide AND_Gate
  assign MEPC_out = 32'hfffffffe;  // AND_Gate MEPC, 32 bits wide AND_Gate
  assign MCAUSE_out = 32'h8000000f;  // AND_Gate MCAUSE, 32 bits wide AND_Gate
  assign MTVAL_out = {32{1'b1}};  // AND_Gate MTVAL, 32 bits wide AND_Gate
  assign MSCRATCH_out = {32{1'b1}};  // AND_Gate MSCRATCH, 32 bits wide AND_Gate
  assign MIP_out = 32'h888;  // AND_Gate MIP, 32 bits wide AND_Gate
  assign MIE_out = wr_data & 32'h888;  // AND_Gate MIE, 32 bits wide
  Comparator #(.mode("unsigned"), .width(12)) comparator_3 (
    .a(12'h304), .b(rd_addr), .eq(comparator_3_eq));  // open: gt, lt
  Register #(.width(32)) r_mcause ();  // open: D, en, clk, Q, clr
  Comparator #(.mode("unsigned"), .width(12)) comparator_4 (.b(12'h304), .eq(comparator_4_eq));  // open: a, gt, lt
  Comparator #(.mode("unsigned"), .width(12)) comparator_5 (.b(12'h305), .eq(comparator_5_eq));  // open: a, gt, lt
  Comparator #(.mode("unsigned"), .width(12)) comparator_6 (.b(12'h341), .eq(comparator_6_eq));  // open: a, gt, lt
  Comparator #(.mode("unsigned"), .width(12)) comparator_7 (.b(12'h342), .eq(comparator_7_eq));  // open: a, gt, lt
  Comparator #(.mode("unsigned"), .width(12)) comparator_8 (.b(12'h343), .eq(comparator_8_eq));  // open: a, gt, lt
  Comparator #(.mode("unsigned"), .width(12)) comparator_9 (.b(12'h340), .eq(comparator_9_eq));  // open: a, gt, lt
  Comparator #(.mode("unsigned"), .width(12)) comparator_10 (.b(12'h344), .eq(comparator_10_eq));  // open: a, gt, lt
  and and_7 (and_7_out, comparator_3_eq, wr_en);
  and and_8 (and_8_out, priority_encoder_1_gs, ~multiplexer_1_out[1], ~multiplexer_1_out[0]);  // AND_Gate
  Multiplexer multiplexer_5 (
    .in0(priority_encoder_1_gs), .in1(comparator_11_eq), .out(multiplexer_5_out), .sel(and_8_out));
  Comparator #(.mode("unsigned"), .width(12)) comparator_11 (
    .a(wr_addr), .b(12'h300), .eq(comparator_11_eq));  // open: gt, lt
  Multiplexer #(.width(32)) multiplexer_6 (.in0(r_mie_q), .in1(MIE_out), .out(multiplexer_6_out), .sel(and_7_out));
  Multiplexer #(.select(2), .width(32)) multiplexer_7 (
    .in0(MIE_out), .in1(r_mie_q), .in2(r_mie_q), .in3({32{1'b0}}), .out(multiplexer_7_out),
    .sel(multiplexer_1_out));
  Register #(.width(32)) r_mie (.D(multiplexer_7_out), .en(multiplexer_5_out), .clk(clk), .Q(r_mie_q), .clr(1'b0));
  Register #(.width(32)) r_mtval ();  // open: D, en, clk, Q, clr
  Register #(.width(32)) r_mip ();  // open: D, en, clk, Q, clr
endmodule
